// Logisim project XEL-4.circ as structural Verilog: 7 circuits, main circuit main
module main (
  input  [3:0] A,
  input  S,
  input  [3:0] STR,
  input  [3:0] REG,
  input  [3:0] REG_2,
  input  C,
  input  SET,
  input  in_8,
  input  in_9,
  input  [3:0] in_10,
  input  in_11,
  input  [3:0] in_12,
  input  in_13,
  input  I1,
  input  I2,
  input  I3,
  input  I4,
  input  C1,
  input  C2,
  input  S_2,
  output [3:0] R,
  output [3:0] OUT,
  output out_23,
  output D1,
  output D2,
  output D3,
  output D4
);

  wire A1, A2, A3, A4, and_1_out, and_2_out, and_3_out, and_4_out, and_5_out, and_6_out, and_7_out,
       and_8_out, and_9_out, and_10_out, and_11_out, and_12_out, and_13_out, and_14_out, and_15_out,
       and_16_out, and_17_out, and_18_out, and_19_out, and_20_out, and_21_out, and_22_out, and_23_out,
       and_24_out, and_25_out, and_26_out, and_27_out, and_28_out, and_29_out, and_30_out, and_31_out,
       and_32_out, and_33_out, and_34_out, and_35_out, and_36_out, B1, B2, B3, B4, C1_t, C2_t, C3, C4, C_t,
       n4_bit_ram_4_s1, n4_bit_ram_4_s2, n4_bit_ram_4_s3, n4_bit_ram_4_s4, not_1_out, not_2_out, not_3_out,
       not_5_out, not_6_out, not_7_out, not_8_out;

  and and_1 (and_1_out, I1, C1, not_1_out);
  and and_2 (and_2_out, I2, C1, not_1_out);
  and and_3 (and_3_out, I3, C1, not_1_out);
  and and_4 (and_4_out, I4, C1, not_1_out);
  not not_1 (not_1_out, C2);
  _4_BIT_RAM u_4_bit_ram_1 (
    .CLEAR(and_5_out), .A1(and_1_out), .A2(and_2_out), .A3(and_3_out), .A4(and_4_out), .S1(A1), .S2(A2),
    .S3(A3), .S4(A4));
  and and_5 (and_5_out, not_1_out, S_2, C1);
  _4_BIT_ADD_SUB u_4_bit_add_sub_1 ();  // open: ADD_SUB, A, B, SUM, ERROR
  not not_2 (not_2_out, C1);
  and and_6 (and_6_out, I1, not_2_out, C2);
  and and_7 (and_7_out, I2, not_2_out, C2);
  and and_8 (and_8_out, I3, not_2_out, C2);
  and and_9 (and_9_out, C2, S_2, C2);
  and and_10 (and_10_out, I4, not_2_out, C2);
  _4_BIT_RAM u_4_bit_ram_2 (
    .CLEAR(and_9_out), .A1(and_6_out), .A2(and_7_out), .A3(and_8_out), .A4(and_10_out), .S1(B1), .S2(B2),
    .S3(B3), .S4(B4));
  assign OUT = 1'b1 ? STR : 4'bz;  // Controlled_Buffer controlled_buffer_1
  and and_11 (and_11_out, I1, C1, C2);
  and and_12 (and_12_out, I2, C1, C2);
  and and_13 (and_13_out, I3, C1, C2);
  and and_14 (and_14_out, I4, C1, C2);
  not not_3 (not_3_out, 1'b1);
  _4_BIT_RAM u_4_bit_ram_3 (
    .CLEAR(and_15_out), .A1(and_11_out), .A2(and_12_out), .A3(and_13_out), .A4(and_14_out), .S1(C1_t),
    .S2(C2_t), .S3(C3), .S4(C4));
  and and_15 (and_15_out, C1, S_2, C2);
  RAM #(.addrWidth(4), .dataWidth(4)) ram_1 (.addr(REG_2), .data(OUT), .clk(SET), .ld(not_3_out));  // open: sel, clr
  not not_4 (C_t, C1);
  not not_5 (not_5_out, C2);
  not not_6 (not_6_out, C1);
  and and_16 (and_16_out, I1, C_t, not_5_out);
  and and_17 (and_17_out, I2, C_t, not_5_out);
  and and_18 (and_18_out, I3, C_t, not_5_out);
  and and_19 (and_19_out, I4, C_t, not_5_out);
  not not_7 (not_7_out, C1);
  and and_20 (and_20_out, not_5_out, S_2, C_t);
  _4_BIT_RAM u_4_bit_ram_4 (
    .CLEAR(and_20_out), .A1(and_16_out), .A2(and_17_out), .A3(and_18_out), .A4(and_19_out),
    .S1(n4_bit_ram_4_s1), .S2(n4_bit_ram_4_s2), .S3(n4_bit_ram_4_s3), .S4(n4_bit_ram_4_s4));
  and and_21 (and_21_out, n4_bit_ram_4_s1, not_5_out, not_7_out);
  and and_22 (and_22_out, n4_bit_ram_4_s2, not_5_out, not_7_out);
  and and_23 (and_23_out, n4_bit_ram_4_s3, not_5_out, not_7_out);
  and and_24 (and_24_out, n4_bit_ram_4_s4, not_5_out, not_7_out);
  and and_25 (and_25_out, A1, C1, not_5_out);
  and and_26 (and_26_out, A2, C1, not_5_out);
  and and_27 (and_27_out, A3, C1, not_5_out);
  and and_28 (and_28_out, A4, C1, not_5_out);
  and and_29 (and_29_out, not_6_out, C2, B1);
  and and_30 (and_30_out, not_6_out, C2, B2);
  and and_31 (and_31_out, not_6_out, C2, B3);
  and and_32 (and_32_out, not_6_out, C2, B4);
  and and_33 (and_33_out, C2, C1, C1_t);
  and and_34 (and_34_out, C2, C1, C2_t);
  and and_35 (and_35_out, C2, C1, C3);
  and and_36 (and_36_out, C2, C1, C4);
  assign R = S ? A : 4'bz;  // Controlled_Buffer controlled_buffer_2
  not not_8 (not_8_out, S);
  EQUAL equal_1 (
    .A1(in_10[0]), .A2(in_10[1]), .A3(in_10[2]), .A4(in_10[3]), .B1(in_12[0]), .B2(in_12[1]), .B3(in_12[2]),
    .B4(in_12[3]), .E(out_23));
  or or_1 (D1, and_21_out, and_25_out, and_29_out, and_33_out);
  or or_2 (D2, and_22_out, and_26_out, and_30_out, and_34_out);
  or or_3 (D3, and_23_out, and_27_out, and_31_out, and_35_out);
  or or_4 (D4, and_24_out, and_28_out, and_32_out, and_36_out);
  RAM #(.addrWidth(4), .dataWidth(4)) ram_2 (.addr(REG), .data(R), .clk(C), .ld(not_8_out));  // open: sel, clr
  DotMatrix #(.matrixcols(1), .matrixrows(4)) dotmatrix_1 (.col0({in_13, in_11, in_9, in_8}));

  // Notes on the sheet:
  //   PROTOTYPE 2-BYTES OF RAM
  //   4x16 RAM
  //   EQUAL TO
endmodule

module FULL_ADDER (
  input  A,
  input  B,
  input  C,
  output S,
  output C_2
);

  wire and_1_out, and_2_out, xor_1_out;

  and and_1 (and_1_out, B, A);
  xor xor_1 (xor_1_out, A, B);
  xor xor_2 (S, xor_1_out, C);
  and and_2 (and_2_out, C, xor_1_out);
  or or_1 (C_2, and_2_out, and_1_out);
endmodule

module SR_LATCH (
  input  A,
  input  B,
  output S1
);

  wire nor_2_out;

  nor nor_1 (S1, A, nor_2_out);
  nor nor_2 (nor_2_out, S1, B);
endmodule

module COMPARATOR (
  input  A,
  input  B,
  output E
);

  wire and_1_out, and_2_out, not_1_out, not_2_out;

  not not_1 (not_1_out, A);
  and and_1 (and_1_out, not_1_out, B);
  and and_2 (and_2_out, A, not_2_out);
  not not_2 (not_2_out, B);
  nor nor_1 (E, and_1_out, and_2_out);
endmodule

module _4_BIT_RAM (
  input  CLEAR,
  input  A1,
  input  A2,
  input  A3,
  input  A4,
  output S1,
  output S2,
  output S3,
  output S4
);

  wire and_1_out, and_2_out, and_3_out, and_4_out, and_5_out, not_1_out;

  and and_1 (and_1_out, not_1_out, A1);
  and and_2 (and_2_out, not_1_out, A2);
  and and_3 (and_3_out, not_1_out, A3);
  and and_4 (and_4_out, not_1_out, A4);
  SR_LATCH sr_latch_1 (.A(CLEAR), .B(and_1_out), .S1(S1));
  SR_LATCH sr_latch_2 (.A(CLEAR), .B(and_2_out), .S1(S2));
  SR_LATCH sr_latch_3 (.A(CLEAR), .B(and_3_out), .S1(S3));
  SR_LATCH sr_latch_4 (.A(CLEAR), .B(and_4_out), .S1(S4));
  and and_5 (and_5_out, S1, S2, S3, S4);
  not not_1 (not_1_out, and_5_out);
endmodule

module EQUAL (
  input  A1,
  input  A2,
  input  A3,
  input  A4,
  input  B1,
  input  B2,
  input  B3,
  input  B4,
  output E
);

  wire comparator_1_e, comparator_2_e, comparator_3_e, comparator_4_e;

  COMPARATOR comparator_1 (.A(A1), .B(B1), .E(comparator_1_e));
  COMPARATOR comparator_2 (.A(A2), .B(B2), .E(comparator_2_e));
  and and_1 (E, comparator_1_e, comparator_2_e, comparator_3_e, comparator_4_e);
  COMPARATOR comparator_3 (.A(A3), .B(B3), .E(comparator_3_e));
  COMPARATOR comparator_4 (.A(A4), .B(B4), .E(comparator_4_e));
endmodule

module _4_BIT_ADD_SUB (
  input  ADD_SUB,
  input  [3:0] A,
  input  [3:0] B,
  output [3:0] SUM,
  output ERROR
);

  wire and_1_out, and_2_out, full_adder_1_c_2, full_adder_2_c_2, full_adder_3_c_2, full_adder_4_c_2,
       not_1_out, not_2_out, xor_1_out, xor_2_out, xor_3_out, xor_4_out;

  xor xor_1 (xor_1_out, B[0], ADD_SUB);
  xor xor_2 (xor_2_out, B[1], ADD_SUB);
  xor xor_3 (xor_3_out, B[2], ADD_SUB);
  xor xor_4 (xor_4_out, B[3], ADD_SUB);
  FULL_ADDER full_adder_1 (.A(A[0]), .B(xor_1_out), .C(ADD_SUB), .S(SUM[0]), .C_2(full_adder_1_c_2));
  FULL_ADDER full_adder_2 (.A(A[1]), .B(xor_2_out), .C(full_adder_1_c_2), .S(SUM[1]), .C_2(full_adder_2_c_2));
  FULL_ADDER full_adder_3 (.A(A[2]), .B(xor_3_out), .C(full_adder_2_c_2), .S(SUM[2]), .C_2(full_adder_3_c_2));
  FULL_ADDER full_adder_4 (.A(A[3]), .B(xor_4_out), .C(full_adder_3_c_2), .S(SUM[3]), .C_2(full_adder_4_c_2));
  not not_1 (not_1_out, full_adder_4_c_2);
  and and_1 (and_1_out, not_1_out, A[0]);
  not not_2 (not_2_out, A[0]);
  and and_2 (and_2_out, not_2_out, full_adder_4_c_2);
  or or_1 (ERROR, and_1_out, and_2_out);
endmodule
